# Fritzing sketch wiring (saved by Fritzing 0.9.3b)

parts:
  Raspberry_Pi_1 = Raspberry Pi 3 [part_number=RPI-3-V1.2]
  U1 = LM 358 Dual Op-Amp [package="DIP8 [THT]"]
  R2 = Resistor [tolerance=±5% resistance=470 package=THT]
  R1 = Resistor [tolerance=±5% resistance=220 package=THT]
  J2 = male pin header, 4 pins [form="♂ (male)" part_number=UART]
  R3 = Resistor [tolerance=±5% resistance=470 package=THT]
  R4 = Resistor [tolerance=±5% resistance=220 package=THT]
  S1 = Pushbutton [package="[THT]"]
  C1 = Electrolytic Capacitor [capacitance=1µF package="100 mil [THT, electrolytic]"]
  J3 = Camdenboss CTB0158-4 [part_number=CTB0158-4 package=THT]
  J5 = female pin header, 4 pins [form="♀ (female)"]
  R5 = Resistor [tolerance=±5% resistance=220 package=THT]
  R6 = Resistor [tolerance=±5% resistance=220 package=THT]
  R8 = Resistor [tolerance=±5% resistance=1k package=THT]
  U3 = mystery part, 3 pins [chip_label="Capteur Proxy"]
  U4 = mystery part, 3 pins [chip_label="Capteur Proxy"]
  U5 = mystery part, 3 pins [chip_label="Capteur Proxy"]
  U6 = mystery part, 3 pins [chip_label="Capteur Proxy"]
  U7 = mystery part, 3 pins [chip_label="Capteur Proxy"]
  R11 = Resistor [tolerance=±5% resistance=220 package=THT]
  R12 = Resistor [tolerance=±5% resistance=220 package=THT]
  R13 = Resistor [tolerance=±5% resistance=470 package=THT]
  R14 = Resistor [tolerance=±5% resistance=470 package=THT]
  R15 = Resistor [tolerance=±5% resistance=220 package=THT]
  R16 = Resistor [tolerance=±5% resistance=470 package=THT]
  R17 = Resistor [tolerance=±5% resistance=470 package=THT]
  R18 = Resistor [tolerance=±5% resistance=220 package=THT]
  R19 = Resistor [tolerance=±5% resistance=220 package=THT]
  R20 = Resistor [tolerance=±5% resistance=470 package=THT]
  U8 = mystery part, 3 pins [chip_label="Capteur Proxy"]
  R21 = Resistor [tolerance=±5% resistance=470 package=THT]
  R22 = Resistor [tolerance=±5% resistance=220 package=THT]
  J8 = female pin header, 3 pins [form="♀ (female)"]
  J9 = female pin header, 3 pins [form="♀ (female)"]
  U2 = LM124-324 Quad Opamp [package="DIP (Dual Inline)"]
  R23 = Resistor [tolerance=±5% resistance=1k package=THT]
  R24 = Resistor [tolerance=±5% resistance=1k package=THT]
  R25 = Resistor [tolerance=±5% resistance=1k package=THT]
  J10 = female pin header, 4 pins [form="♀ (female)"]
  J11 = female pin header, 4 pins [form="♀ (female)"]
  J12 = female pin header, 4 pins [form="♀ (female)"]

nets:
  N1: Raspberry_Pi_1.GND, U1.connector3, R2.Pin_1, J2.pin3, R4.Pin_0, S1.Pin_3, C1.-, J3.pin4, U3.pin1, U4.pin1, U5.pin1, U6.pin1, U7.pin1, R13.Pin_0, R14.Pin_0, R16.Pin_0, R17.Pin_0, R20.Pin_0, R21.Pin_0, J8.pin1
  N2: Raspberry_Pi_1.GIPO5, R11.Pin_0, R14.Pin_1
  N3: Raspberry_Pi_1.GIPO6, R12.Pin_0, R13.Pin_1
  N4: Raspberry_Pi_1.GIPO13, R15.Pin_0, R16.Pin_1
  N5: Raspberry_Pi_1.GIPO19, R17.Pin_1, R18.Pin_0
  N6: Raspberry_Pi_1.GIPO26, R19.Pin_0, R20.Pin_1
  N7: Raspberry_Pi_1.GIPO21, S1.Pin_1
  N8: Raspberry_Pi_1.GIPO12, R21.Pin_1, R22.Pin_0
  N9: Raspberry_Pi_1.GIPO15, R2.Pin_0, R1.Pin_0
  N10: Raspberry_Pi_1.GIPO14, U1.connector2
  N11: Raspberry_Pi_1.5V, U1.connector7, C1.+, J3.pin2, U3.pin3, U4.pin3, U5.pin3, U6.pin3, U7.pin3, J8.pin3
  N12: U1.connector0, J2.pin2
  N13: U1.connector1, R3.Pin_1, R4.Pin_1
  N14: R1.Pin_1, J2.pin4
  N15: J2.pin1, R3.Pin_0
  N16: J3.pin1, J5.pin4, R5.Pin_1, R8.Pin_1, U2.VCC+, R23.Pin_1, R24.Pin_0, R25.Pin_0, J10.pin4, J11.pin4, J12.pin4
  N17: J5.pin1, R6.Pin_1, U2.VCC-, J10.pin1
  N18: J5.pin2, U2.3IN+, R23.Pin_0
  N19: J5.pin3, U2.2IN+, R24.Pin_1
  N20: R5.Pin_0, R6.Pin_0
  N21: R8.Pin_0, U2.4IN+, J10.pin2
  N22: U3.pin2, R12.Pin_1
  N23: U4.pin2, R11.Pin_1
  N24: U5.pin2, R15.Pin_1
  N25: U6.pin2, R18.Pin_1
  N26: U7.pin2, R19.Pin_1
  N27: U8.pin1, J9.pin1
  N28: U8.pin2, J9.pin2
  N29: U8.pin3, J9.pin3
  N30: R22.Pin_1, J8.pin2
  N31: U2.1OUT, J11.pin3
  N32: U2.1IN-, U2.2IN-
  N33: U2.1IN+, R25.Pin_1, J10.pin3
  N34: U2.2OUT, J12.pin3
  N35: U2.3OUT, J12.pin2
  N36: U2.3IN-, U2.4IN-
  N37: U2.4OUT, J11.pin2
